// Logisim project CPU(S-MIPS).circ as structural Verilog: 1 circuit, main circuit S-MIPS
module S_MIPS (
  input  [31:0] RAM_Out_0,
  input  [31:0] RAM_Out_1,
  input  [31:0] RAM_Out_2,
  input  [31:0] RAM_Out_3,
  input  [3:0] Read_Time,
  input  [3:0] Write_Time,
  input  Reset,
  input  Clock,
  input  Kbd_Available,
  input  [6:0] Kbd_ASCII_Data,
  output [31:0] RAM_In_0,
  output [31:0] RAM_In_1,
  output [31:0] RAM_In_2,
  output [31:0] RAM_In_3,
  output Halt,
  output [15:0] Address,
  output Kbd_Enable,
  output Kbd_Clear,
  output TTY_Enable,
  output [6:0] TTY_ASCII_Data,
  output [3:0] Mask,
  output nRead_Write,
  output Chip_Select
);

  wire control_unit_1_fetch, control_unit_1_reset_2, fetched, Start;

  Control_Unit control_unit_1 (
    .START(Start), .FETCHED(fetched), .HALT(Halt), .RESET(Reset), .fetch(control_unit_1_fetch),
    .reset_2(control_unit_1_reset_2));  // open: EXECUTED, Instruction_Type
  DataPath datapath_1 (
    .reset(control_unit_1_reset_2), .fetch(control_unit_1_fetch), .KBD_Data(Kbd_ASCII_Data),
    .KBD_Enable(Kbd_Available), .TTY_Enable(TTY_Enable), .TTY_Data(TTY_ASCII_Data), .fetched(fetched),
    .halt(Halt));

  // Other names for the same wires on the sheet: CLK = Clock; CLR = Reset; CS = Chip_Select;
  //   KBD_AVAIL = Kbd_Available; KBD_CLR = Kbd_Clear; KBD_DATA[6:0] = Kbd_ASCII_Data; RAM_A[15:0] = Address;
  //   RAM_INPUT_0[31:0] = RAM_In_0; RAM_INPUT_1[31:0] = RAM_In_1; RAM_INPUT_2[31:0] = RAM_In_2;
  //   RAM_INPUT_3[31:0] = RAM_In_3; RAM_MASK[3:0] = Mask; RAM_OUTPUT_0[31:0] = RAM_Out_0;
  //   RAM_OUTPUT_1[31:0] = RAM_Out_1; RAM_OUTPUT_2[31:0] = RAM_Out_2; RAM_OUTPUT_3[31:0] = RAM_Out_3;
  //   RW = nRead_Write; STOP = Halt; TTY_DATA[6:0] = TTY_ASCII_Data

  // Notes on the sheet:
  //   RAM TIMING
  //   KEYBOARD
  //   DATA FROM RAM
  //   RAM ADDRESS
  //   KEYBOARD
  //   TTY
  //   DATA WRITE MASK
  //   RAM CONTROL
  //   DATA TO RAM
endmodule
