// Logisim project Control_Unit.circ as structural Verilog: 1 circuit, main circuit Control Unit
module Control_Unit (
  input  [5:0] FuncCode,
  input  [5:0] OpCode,
  input  START,
  input  Clock,
  input  RamReady,
  output [17:0] SelectorCodes,
  output [2:0] FC_Selector,
  output [3:0] ALU_Op,
  output fetch,
  output rnd_kbd_Selector,
  output TTY_Enable,
  output ReadInstruction,
  output ChipSelect,
  output R_W,
  output halt,
  output kbd_Enable,
  output RESET
);

  wire CS1, CS2, CS3, CS4, demultiplexer_1_out0, demultiplexer_1_out1, demultiplexer_2_out0,
       demultiplexer_3_out0, demultiplexer_4_out0, demultiplexer_5_out0, demultiplexer_6_out0, FETCH_q,
       IDLE_q, Load, Main, or_1_out, or_7_out, Pop, Push, R1, R2, R2_1, R3, R4, ReadMemory_2_q, ReadMemory_q,
       Store, WriteMemory_2_q;
  wire [1:0] SS_Code;
  wire [17:0] F_S_Codes;

  or or_1 (or_1_out, demultiplexer_1_out0, 1'b1);
  not not_1 (RESET, START);
  or or_2 (R_W, Push, Store);
  D_Flip_Flop IDLE (.clk(Clock), .D(or_1_out), .Q(IDLE_q), .preset(RESET));  // open: Qn, en, reset
  Demultiplexer #(.enable("false")) demultiplexer_1 (
    .out0(demultiplexer_1_out0), .out1(demultiplexer_1_out1), .in(IDLE_q), .sel(RESET));
  Priority_Encoder #(.select(2)) priority_encoder_1 (
    .in0(R1), .in1(R2), .in2(R3), .in3(Main), .out(SS_Code));  // open: gs, en_out, en_in
  or or_3 (CS1, demultiplexer_2_out0, Pop);
  or or_4 (CS2, demultiplexer_3_out0, Push);
  or or_5 (CS3, demultiplexer_4_out0, Load);
  or or_6 (CS4, demultiplexer_5_out0, Store);
  or or_7 (or_7_out, R1, R2_1, R3, R4, Main);
  or or_8 (fetch, demultiplexer_6_out0, or_7_out, demultiplexer_1_out1);
  D_Flip_Flop ReadMemory (.clk(Clock), .D(CS1), .Q(ReadMemory_q));  // open: Qn, preset, en, reset
  D_Flip_Flop WriteMemory (.clk(Clock), .D(CS2), .Q(R2));  // open: Qn, preset, en, reset
  D_Flip_Flop ReadMemory_2 (.clk(Clock), .D(CS3), .Q(ReadMemory_2_q));  // open: Qn, preset, en, reset
  D_Flip_Flop WriteMemory_2 (.clk(Clock), .D(CS4), .Q(WriteMemory_2_q));  // open: Qn, preset, en, reset
  D_Flip_Flop #(.trigger("falling")) u_FETCH (
    .clk(Clock), .D(fetch), .Q(FETCH_q), .reset(RESET));  // open: Qn, preset, en
  Demultiplexer #(.enable("false")) demultiplexer_2 (
    .out0(demultiplexer_2_out0), .out1(R1), .in(ReadMemory_q), .sel(RamReady));
  Demultiplexer #(.enable("false")) demultiplexer_3 (.out0(demultiplexer_3_out0), .out1(R2_1), .in(R2), .sel(RamReady));
  Demultiplexer #(.enable("false")) demultiplexer_4 (
    .out0(demultiplexer_4_out0), .out1(R3), .in(ReadMemory_2_q), .sel(RamReady));
  Demultiplexer #(.enable("false")) demultiplexer_5 (
    .out0(demultiplexer_5_out0), .out1(R4), .in(WriteMemory_2_q), .sel(RamReady));
  Demultiplexer #(.enable("false")) demultiplexer_6 (
    .out0(demultiplexer_6_out0), .out1(ReadInstruction), .in(FETCH_q), .sel(RamReady));
  Multiplexer #(.select(2), .width(18), .enable("false")) multiplexer_1 (
    .in0(SelectorCodes), .in1(18'h20024), .in2(18'h10), .in3(18'h20021), .out(F_S_Codes), .sel(SS_Code));
  // Switcher_CU switcher_cu_1: pin names not known; wires that end beside it: FuncCode, ReadInstruction, OpCode, kbd_Enable, FC_Selector, ALU_Op, SelectorCodes, Pop, Push, Main, Load, Store, TTY_Enable, rnd_kbd_Selector, halt
  or or_9 (ChipSelect, CS4, CS3, CS2, CS1, fetch);

  // Other names for the same wires on the sheet: Chip_Select = ChipSelect; clk = Clock; CS0 = fetch;
  //   ReadIns = ReadInstruction; Selector_Codes[17:0] = SelectorCodes

  // Notes on the sheet:
  //   Input_Output_Region
  //   Instruction-Lines
endmodule
